# Fritzing sketch OLEDOnBreadboard (saved by Fritzing 0.9.3b)
breadboards: 1

parts:
  Part1 = OLED Monochrome 128x64 1.3 inch [part_number=938]
  Netduino1 = Netduino Plus2

nets:
  N1: Part1.MOSI_SDA, Netduino1.SD
  N2: Part1.SCLK_SCK, Netduino1.SC
  VIN: Part1.VIN, Netduino1.3V3
  GND: Part1.GND, Netduino1.GND

custom parts:
  OLED Monochrome 128x64 1.3 inch: These displays are small, only about 1.3" diagonal, but very readable due to the high contrast of an OLED display. This display is made of 128x64 individual white OLED pixels, each one is turned on or off by the controller chip. Because the display makes its own light, no backlight is required. This reduces the power required to run the OLED and is why the display has such high contrast; we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
