# Fritzing sketch BNO055OnBreadboard (saved by Fritzing 0.9.3b)
breadboards: 1

parts:
  Netduino1 = Netduino Plus2
  Part1 = 9-DOF Absolute Orientation IMU Fusion Breakout - BNO055

nets:
  N1: Netduino1.D8_CTS1, Part1.RST_5V
  N2: Netduino1.3V3, Part1.5.0V
  GND: Netduino1.GND, Part1.GND
  N3: Netduino1.SC, Part1.SCL_5V
  N4: Netduino1.SD, Part1.SDA_5V

custom parts:
  9-DOF Absolute Orientation IMU Fusion Breakout - BNO055: A MEMS accelerometer, magnetometer and gyroscope on a single die with a high speed ARM Cortex-M0 based processor to digest all the sensor data, abstract the sensor fusion and real time requirements away, and spit out data you can use in quaternions, Euler angles or vectors.
