# Fritzing sketch Si1145OnBreadboard (saved by Fritzing 0.9.3b)
breadboards: 1

parts:
  Part1 = SI1145 Digital UV Index + IR + Visible Light Sensor [part_number=1777]
  Netduino1 = Netduino Plus2

nets:
  +5V: Part1.+5V, Netduino1.3V3
  GND: Part1.GND, Netduino1.GND
  N1: Part1.SCL, Netduino1.SC
  N2: Part1.SDA, Netduino1.SD

custom parts:
  SI1145 Digital UV Index + IR + Visible Light Sensor: The SI1145 is a new sensor from SiLabs with a calibrated light sensing algorithm that can calculate UV Index. It doesn't contain an actual UV sensing element, instead it approximates it based on visible & IR light from the sun. We took this outside a couple days and compared the calculated UV index with the news-reported index and found it was very accurate! It's a digital sensor that works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
