# Fritzing sketch SparkfunADXL345OnBreadboard (saved by Fritzing 0.9.3b)
breadboards: 1

parts:
  Netduino_1 = Netduino 2
  Part1 = Triple Axis Accelerometer Breakout - ADXL345
  R1 = Resistor [tolerance=±5% resistance=4.7k package=THT]
  R2 = Resistor [tolerance=±5% resistance=4.7k package=THT]

nets:
  3V3: Netduino_1.3V3, Part1.VCC, Part1.CS, R1.Pin_0, R2.Pin_0
  GND: Netduino_1.GND, Part1.GND, Part1.SDO
  N1: Netduino_1.SCL, Part1.SCL, R1.Pin_1
  N2: Netduino_1.SDA, Part1.SDA, R2.Pin_1

custom parts:
  Netduino 2: An open-source electronics platform using the .NET Micro Framework
