# Fritzing sketch TMP102OnBreadboard (saved by Fritzing 0.9.3b)
breadboards: 1

parts:
  Netduino1 = Netduino Plus2
  Part1 = Digital Temperature Sensor Breakout - TMP102

nets:
  N1: Netduino1.3V3, Part1.V+
  GND: Netduino1.GND, Part1.GND
  N2: Netduino1.SC, Part1.SCL
  N3: Netduino1.SD, Part1.SDA
