# Fritzing sketch RgbPwmLed (saved by Fritzing 0.9.3b)
breadboards: 1

parts:
  Netduino1 = Netduino Plus2
  R1 = Resistor [tolerance=±5% resistance=4.7 package=THT]
  R2 = Resistor [tolerance=±5% resistance=4.7 package=THT]
  LED1 = RGB LED (com. cathode, rgb) [package="5 mm [THT]"]
  R3 = Resistor [tolerance=±5% resistance=47 package=THT]

nets:
  N1: Netduino1.GND, LED1.common_cathode
  N2: Netduino1.D11_MOSI, R2.Pin_0
  N3: Netduino1.D10_PWM3, R1.Pin_0
  N4: Netduino1.D9_PWM2, R3.Pin_0
  N5: R1.Pin_1, LED1.green_anode
  N6: R2.Pin_1, LED1.blue_anode
  N7: LED1.red_anode, R3.Pin_1
