# Fritzing sketch Led (saved by Fritzing 0.9.3b)
breadboards: 1

parts:
  LED4 = LED - 3mm [color="Red (633nm)" package="3 mm [THT]"]
  Netduino1 = Netduino Plus2
  R1 = Resistor [tolerance=±5% resistance=220 package=THT]

nets:
  N1: LED4.cathode, Netduino1.GND
  N2: LED4.anode, R1.Pin_1
  N3: Netduino1.D8_CTS1, R1.Pin_0
