# Fritzing sketch PwmLed (saved by Fritzing 0.9.3b)

parts:
  Netduino1 = Netduino Plus2
  LED1 = LED - 5mm [color="Green (570nm)" package="5 mm [THT]"]

nets:
  N1: Netduino1.D11_MOSI, LED1.anode
  N2: Netduino1.GND, LED1.cathode
