# Fritzing sketch RgbPwmLed (saved by Fritzing 0.9.3b)
breadboards: 1

parts:
  Netduino1 = Netduino Plus2
  LED1 = RGB LED (com. cathode, rgb) [package="5 mm [THT]"]

nets:
  N1: Netduino1.GND, LED1.common_cathode
  N2: Netduino1.D11_MOSI, LED1.blue_anode
  N3: Netduino1.D10_PWM3, LED1.green_anode
  N4: Netduino1.D9_PWM2, LED1.red_anode
