# Fritzing sketch DualMotorHBridge (saved by Fritzing 0.9.3b)
breadboards: 1

parts:
  M1 = DC Motor
  Netduino1 = Netduino Plus2
  IC1 = H-Bridge [package=THT]
  VCC1 = 4 x AAA Battery Mount
  M2 = DC Motor

nets:
  N1: M1.pin_1, IC1.1Y
  N2: M1.pin_2, IC1.2Y
  GND: Netduino1.GND, IC1.GND1, IC1.GND2, IC1.GND3, IC1.GND4, VCC1.-
  N3: Netduino1.D10_PWM3, IC1.4A
  N4: Netduino1.D7_RTS1, IC1.3_4EN
  N5: Netduino1.D6_PWM1, IC1.3A
  N6: Netduino1.D5_PWM0, IC1.2A
  N7: Netduino1.D4_CS0, IC1.1_2EN
  N8: Netduino1.D3_TX1, IC1.1A
  N9: Netduino1.+5V, IC1.VCC1
  N10: IC1.VCC2, VCC1.+
  N11: IC1.3Y, M2.pin_1
  N12: IC1.4Y, M2.pin_2
