# Fritzing sketch PushButton (saved by Fritzing 0.9.3b)
breadboards: 1

parts:
  S1 = Pushbutton [package="[THT]"]
  Netduino1 = Netduino

nets:
  N1: S1.Pin_1, S1.Pin_2, Netduino1.GND
  N2: S1.Pin_3, S1.Pin_4, Netduino1.D0_RX0
