# Fritzing sketch RotaryEncoder_LEDDimmer (saved by Fritzing 0.9.3b)
breadboards: 1

parts:
  Netduino1 = Netduino Plus2
  RE1 = Rotary Encoder [package=THT]
  LED1 = LED - 5mm [color="Green (570nm)" package="5 mm [THT]"]

nets:
  N1: Netduino1.GND, LED1.cathode
  N2: Netduino1.D11_MOSI, LED1.anode
  N3: Netduino1.D7_RTS1, RE1.EncoderPinB
  N4: Netduino1.D6_PWM1, RE1.EncoderPinA
  N5: Netduino1.3V3, RE1.EncoderPinC
