# Fritzing sketch 8PositionDipSwitch (saved by Fritzing 0.9.3b)
breadboards: 1

parts:
  Netduino1 = Netduino Plus2
  SW1 = DIP Switch 8 Position [package=dipswitch-08]

nets:
  N1: Netduino1.GND, SW1.9, SW1.10, SW1.11, SW1.12, SW1.13, SW1.14, SW1.15, SW1.16
  N2: Netduino1.D7_RTS1, SW1.1
  N3: Netduino1.D6_PWM1, SW1.2
  N4: Netduino1.D5_PWM0, SW1.3
  N5: Netduino1.D4_CS0, SW1.4
  N6: Netduino1.D3_TX1, SW1.5
  N7: Netduino1.D2_RX1, SW1.6
  N8: Netduino1.D1_TX0, SW1.7
  N9: Netduino1.D0_RX0, SW1.8
