# Fritzing sketch TMP36 (saved by Fritzing 0.9.3b)
breadboards: 1

parts:
  Netduino_1 = Netduino 2
  U1 = TMP36 [package=to-92]

nets:
  3V3: Netduino_1.3V3, U1.VCC
  GND: Netduino_1.GND, U1.GND
  N1: Netduino_1.A0, U1.VOUT

custom parts:
  Netduino 2: An open-source electronics platform using the .NET Micro Framework
