# Fritzing sketch LCD-MicroLiquidCrystal (saved by Fritzing 0.9.3b)

parts:
  Part1 = Adafruit I2C+SPI LCD Backpack [part_number="Adafruit #292"]
  U1 = LCD-16X2 [package=lcd-16x2_noholes]
  Netduino1 = Netduino

nets:
  GND: Part1.GND, U1.VSS, U1.R_W, Netduino1.GND
  VCC: Part1.VCC, U1.VDD, U1.A, Netduino1.+5V
  N1: Part1.CLOCK, Netduino1.D13_SPCK
  N2: Part1.DATA, Netduino1.D11_MOSI
  N3: Part1.LATCH, Netduino1.D3_TX1
  N4: Part1.CONTRAST, U1.VO
  N5: Part1.RS, U1.RS
  N6: Part1.E, U1.E
  N7: Part1.DB0, U1.DB0
  N8: Part1.DB1, U1.DB1
  N9: Part1.DB2, U1.DB2
  N10: Part1.DB3, U1.DB3
  N11: Part1.DB4, U1.DB4
  N12: Part1.DB5, U1.DB5
  N13: Part1.DB6, U1.DB6
  N14: Part1.DB7, U1.DB7
  N15: Part1.LEDK, U1.K

custom parts:
  Adafruit I2C+SPI LCD Backpack: LCD backpacks reduce the number of pins needed to connect to an LCD. LCDs are a fun and easy way to have your microcontroller project talk back to you. Character LCDs are common, and easy to get, available in tons of colors and sizes. We've written tutorials on using character LCDs with an Arduino (or similar microcontroller) but find that the number of pins necessary to control the LCD can be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
