# Fritzing sketch ShiftRegisterAndLEDs (saved by Fritzing 0.9.3b)
breadboards: 1

parts:
  Netduino1 = Netduino Plus2
  IC1 = SHIFT REGISTER [package=dil16]
  R1 = Resistor [tolerance=±5% resistance=68 package="0603 [SMD]"]
  R2 = Resistor [tolerance=±5% resistance=68 package="0603 [SMD]"]
  R3 = Resistor [tolerance=±5% resistance=68 package="0603 [SMD]"]
  R4 = Resistor [tolerance=±5% resistance=68 package="0603 [SMD]"]
  R5 = Resistor [tolerance=±5% resistance=68 package="0603 [SMD]"]
  R6 = Resistor [tolerance=±5% resistance=68 package="0603 [SMD]"]
  R7 = Resistor [tolerance=±5% resistance=68 package="0603 [SMD]"]
  R8 = Resistor [tolerance=±5% resistance=68 package="0603 [SMD]"]
  LED1 = smd LED [color="Red (633nm)" package="1206 [SMD]"]
  LED2 = smd LED [color="Red (633nm)" package="1206 [SMD]"]
  LED3 = smd LED [color="Red (633nm)" package="1206 [SMD]"]
  LED4 = smd LED [color="Red (633nm)" package="1206 [SMD]"]
  LED5 = smd LED [color="Red (633nm)" package="1206 [SMD]"]
  LED6 = smd LED [color="Red (633nm)" package="1206 [SMD]"]
  LED7 = smd LED [color="Red (633nm)" package="1206 [SMD]"]
  LED8 = smd LED [color="Red (633nm)" package="1206 [SMD]"]

nets:
  N1: Netduino1.D13_SPCK, IC1.SCK
  N2: Netduino1.D11_MOSI, IC1.SER
  N3: Netduino1.D8_CTS1, IC1.RCK
  3V3: Netduino1.3V3, IC1.SCL, IC1.VCC
  GND: Netduino1.GND, IC1.GND, IC1.G, R1.Pin_1, R2.Pin_1, R3.Pin_1, R4.Pin_1, R5.Pin_1, R6.Pin_1, R7.Pin_1, R8.Pin_1
  N4: IC1.QB, LED1.anode
  N5: IC1.QC, LED6.anode
  N6: IC1.QD, LED5.anode
  N7: IC1.QE, LED4.anode
  N8: IC1.QF, LED3.anode
  N9: IC1.QG, LED8.anode
  N10: IC1.QH, LED7.anode
  N11: IC1.QA, LED2.anode
  N12: R1.Pin_0, LED3.cathode
  N13: R2.Pin_0, LED4.cathode
  N14: R3.Pin_0, LED8.cathode
  N15: R4.Pin_0, LED7.cathode
  N16: R5.Pin_0, LED1.cathode
  N17: R6.Pin_0, LED2.cathode
  N18: R7.Pin_0, LED5.cathode
  N19: R8.Pin_0, LED6.cathode
