# Fritzing sketch Output (saved by Fritzing 0.9.3b)
breadboards: 1

parts:
  IC3 = Microchip MCP23008 8-bit I/O expander [part_number=MCP23008 package="DIP (Dual Inline) [THT]"]
  Netduino1 = Netduino Plus2
  LED_8 = LED - 3mm [color="Red (633nm)" package="3 mm [THT]"]
  LED_1 = LED - 3mm [color="Red (633nm)" package="3 mm [THT]"]
  LED_2 = LED - 3mm [color="Red (633nm)" package="3 mm [THT]"]
  LED_3 = LED - 3mm [color="Red (633nm)" package="3 mm [THT]"]
  LED_4 = LED - 3mm [color="Red (633nm)" package="3 mm [THT]"]
  LED_5 = LED - 3mm [color="Red (633nm)" package="3 mm [THT]"]
  LED_6 = LED - 3mm [color="Red (633nm)" package="3 mm [THT]"]
  LED_7 = LED - 3mm [color="Red (633nm)" package="3 mm [THT]"]
  R1 = Resistor [tolerance=±5% resistance=330 package=THT]
  R2 = Resistor [tolerance=±5% resistance=330 package=THT]
  R3 = Resistor [tolerance=±5% resistance=330 package=THT]
  R4 = Resistor [tolerance=±5% resistance=330 package=THT]
  R5 = Resistor [tolerance=±5% resistance=330 package=THT]
  R6 = Resistor [tolerance=±5% resistance=330 package=THT]
  R7 = Resistor [tolerance=±5% resistance=330 package=THT]
  R8 = Resistor [tolerance=±5% resistance=330 package=THT]
  R9 = Resistor [tolerance=±5% resistance=4.7k package=THT]
  R10 = Resistor [tolerance=±5% resistance=4.7k package=THT]

nets:
  N1: IC3.SCL, Netduino1.SC, R10.Pin_1
  N2: IC3.SDA, Netduino1.SD, R9.Pin_1
  VDD: IC3.A2, IC3.A1, IC3.A0, IC3.Reset, IC3.VDD, Netduino1.3V3, R9.Pin_0, R10.Pin_0
  GND: IC3.VSS, Netduino1.GND, R1.Pin_1, R2.Pin_1, R3.Pin_1, R4.Pin_1, R5.Pin_1, R6.Pin_1, R7.Pin_1, R8.Pin_1
  N3: IC3.GP0, LED_1.anode
  N4: IC3.GP1, LED_2.anode
  N5: IC3.GP2, LED_3.anode
  N6: IC3.GP3, LED_4.anode
  N7: IC3.GP4, LED_5.anode
  N8: IC3.GP5, LED_6.anode
  N9: IC3.GP6, LED_7.anode
  N10: IC3.GP7, LED_8.anode
  N11: LED_8.cathode, R8.Pin_0
  N12: LED_1.cathode, R1.Pin_0
  N13: LED_2.cathode, R2.Pin_0
  N14: LED_3.cathode, R3.Pin_0
  N15: LED_4.cathode, R4.Pin_0
  N16: LED_5.cathode, R5.Pin_0
  N17: LED_6.cathode, R6.Pin_0
  N18: LED_7.cathode, R7.Pin_0

custom parts:
  Microchip MCP23008 8-bit I/O expander: Provides 8-bit, general purpose, parallel I/O expansion for I2C bus. Datasheet: http://ww1.microchip.com/downloads/en/devicedoc/21919e.pdf
