# Fritzing sketch Output_w_Relay (saved by Fritzing 0.9.3b)
breadboards: 1

parts:
  IC3 = Microchip MCP23008 8-bit I/O expander [part_number=MCP23008 package="DIP (Dual Inline) [THT]"]
  Netduino1 = Netduino Plus2
  R9 = Resistor [tolerance=±5% resistance=4.7k package=THT]
  R10 = Resistor [tolerance=±5% resistance=4.7k package=THT]
  U1 = RELAY [package=relay-g5q]

nets:
  N1: IC3.SCL, Netduino1.SC, R10.Pin_1
  N2: IC3.SDA, Netduino1.SD, R9.Pin_1
  VDD: IC3.A2, IC3.A1, IC3.A0, IC3.Reset, IC3.VDD, Netduino1.3V3, R9.Pin_0, R10.Pin_0
  GND: IC3.VSS, Netduino1.GND, U1.COIL2
  N3: IC3.GP1, U1.COIL1

custom parts:
  Microchip MCP23008 8-bit I/O expander: Provides 8-bit, general purpose, parallel I/O expansion for I2C bus. Datasheet: http://ww1.microchip.com/downloads/en/devicedoc/21919e.pdf
