# Fritzing sketch MPL115A2OnBreadboardWithShutdown (saved by Fritzing 0.9.3b)
breadboards: 1

parts:
  Part1 = MPL115A2 I2C Barometric Pressure, Temperature Sensor
  Netduino1 = Netduino Plus2

nets:
  VDD: Part1.VDD, Netduino1.3V3
  GND: Part1.GND, Netduino1.GND
  N1: Part1.SCL, Netduino1.SC
  N2: Part1.SDA, Netduino1.SD
  N3: Part1.RESET, Netduino1.D8_CTS1
  N4: Part1.SDWN, Netduino1.D9_PWM2

custom parts:
  MPL115A2 I2C Barometric Pressure, Temperature Sensor: This pressure sensor from Freescale is a great low-cost sensing solution for measuring barometric pressure. At 1.5 hPa resolution, it's not as precise as our favorite pressure sensor, the BMP085, which has up to 0.03 hPa resolution so we don't suggest it as a precision altimeter. However, it's great for basic barometric pressure sensing. The sensor is soldered onto a PCB with 10K pull-up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
