# Fritzing sketch ALS-PT19OnBreadboard (saved by Fritzing 0.9.3b)
breadboards: 1

parts:
  Part1 = ALSPT19315C
  Netduino1 = Netduino Plus2

nets:
  GND: Part1.GND, Netduino1.GND
  N1: Part1.OUT, Netduino1.A3
  VCC: Part1.VCC, Netduino1.3V3

custom parts:
  ALSPT19315C: Add a teeny analog light sensor, the ALS PT19 analog light sensor is a great way to upgrade a project that uses a photocell and needs RoHS compliance. Due to the high rejection ratio of infrared radiation, the spectral response of the ambient light sensor is close to that of human eyes. It's a pretty simple sensor - connect - to ground, + to 2.5V-5.5V or so to power it. Now measure the analog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
