# Fritzing sketch TSL2561 (saved by Fritzing 0.9.3b)
breadboards: 1

parts:
  Netduino_1 = Netduino 2
  Part1 = Adafruit TSL2591 [part_number="Adafruit #1980"]

nets:
  N1: Netduino_1.D7, Part1.INT
  3V3: Netduino_1.3V3, Part1.3.3V
  GND: Netduino_1.GND, Part1.GND
  N2: Netduino_1.SCL, Part1.SCL
  N3: Netduino_1.SDA, Part1.SDA

custom parts:
  Netduino 2: An open-source electronics platform using the .NET Micro Framework
  Adafruit TSL2591: When the future is dazzlingly-bright, this ultra-high-range luminosity sensor will help you measure it. The TSL2591 luminosity sensor is an advanced digital light sensor, ideal for use in a wide range of light situations. Compared to low cost CdS cells, this sensor is more precise, allowing for exact lux calculations and can be configured for different gain/timing ranges to detect light ranges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
