# Fritzing sketch ADXL335OnBreadboard (saved by Fritzing 0.9.3b)
breadboards: 1

parts:
  Part1 = Triple Axis Accelerometer Breakout - ADXL335
  Netduino1 = Netduino Plus2

nets:
  GND: Part1.ST, Part1.GND, Netduino1.GND
  N1: Part1.ZOUT, Netduino1.A0
  N2: Part1.YOUT, Netduino1.A1
  N3: Part1.XOUT, Netduino1.A2
  VCC: Part1.VCC, Netduino1.3V3
