# Fritzing sketch DS18B20OnBreadboard (saved by Fritzing 0.9.3b)
breadboards: 1

parts:
  Netduino1 = Netduino Plus2
  DS1 = DS18B20 1-Wire Temperature Sensor [part_number=DS18B20]

nets:
  N1: Netduino1.D3_TX1, DS1.DQ
  3V3: Netduino1.3V3, DS1.VDD
  GND: Netduino1.GND, DS1.GND
