# Fritzing sketch Servo (saved by Fritzing 0.9.3b)
breadboards: 1

parts:
  J1 = Basic Servo
  Netduino1 = Netduino Plus2
  VCC2 = Battery
  VCC1 = Battery

nets:
  GND: J1.gnd, Netduino1.GND, VCC1.-
  N1: J1.vcc, VCC2.+
  N2: J1.pulse, Netduino1.D9_PWM2
  N3: VCC2.-, VCC1.+
