# Fritzing sketch Servo_Testing (saved by Fritzing 0.9.3b)
breadboards: 1

parts:
  J1 = Basic Servo
  Netduino1 = Netduino Plus2

nets:
  GND: J1.gnd, Netduino1.GND
  VCC: J1.vcc, Netduino1.+5V
  N1: J1.pulse, Netduino1.D9_PWM2
